// Logisim project ALU16-Hack.circ as structural Verilog: 8 circuits, main circuit main
module main (
  input  [7:0] in_1,
  input  in_2,
  input  [7:0] in_3,
  output [7:0] out_4
);

  wire clock_1_out, not_1_out;

  Clock clock_1 (.out(clock_1_out));
  assign out_4 = in_2 ? in_1 : 8'bz;  // Controlled_Buffer controlled_buffer_1
  not not_1 (not_1_out, in_2);
  RAM ram_1 (.addr(in_3), .data(out_4), .clk(clock_1_out), .ld(not_1_out));  // open: sel, clr
endmodule

module ALU (
  input  NX,
  input  NX_2,
  input  ZY,
  input  NY,
  input  F,
  input  NO,
  input  [15:0] X,
  input  [15:0] Y,
  output [15:0] Out,
  output NG,
  output ZR
);

  wire or_1_out;
  wire [15:0] adder_1_out, and_1_out, multiplexer_1_out, multiplexer_2_out, multiplexer_3_out,
       multiplexer_4_out, multiplexer_5_out, not_1_out, not_2_out, not_4_out;

  Multiplexer #(.width(16), .enable("false")) multiplexer_1 (
    .in0(X), .in1({16{1'b0}}), .out(multiplexer_1_out), .sel(NX));
  Multiplexer #(.width(16), .enable("false")) multiplexer_2 (
    .in0(Y), .in1({16{1'b0}}), .out(multiplexer_2_out), .sel(ZY));
  Multiplexer #(.width(16), .enable("false")) multiplexer_3 (
    .in0(multiplexer_1_out), .in1(not_1_out), .out(multiplexer_3_out), .sel(NX_2));
  assign not_1_out = ~multiplexer_1_out;  // NOT_Gate not_1, 16 bits wide
  Multiplexer #(.width(16), .enable("false")) multiplexer_4 (
    .in0(multiplexer_2_out), .in1(not_2_out), .out(multiplexer_4_out), .sel(NY));
  assign not_2_out = ~multiplexer_2_out;  // NOT_Gate not_2, 16 bits wide
  assign and_1_out = multiplexer_3_out & multiplexer_4_out;  // AND_Gate and_1, 16 bits wide
  Adder #(.width(16)) adder_1 (.a(multiplexer_3_out), .b(multiplexer_4_out), .out(adder_1_out));  // open: cin, cout
  or or_1 (or_1_out, NG, Out[14], Out[13], Out[12], Out[11], Out[10], Out[9], Out[8], Out[7], Out[6], Out[5], Out[4], Out[3], Out[2], Out[1], Out[0]);
  not not_3 (ZR, or_1_out);
  Multiplexer #(.width(16), .enable("false")) multiplexer_5 (
    .in0(and_1_out), .in1(adder_1_out), .out(multiplexer_5_out), .sel(F));
  Multiplexer #(.width(16), .enable("false")) multiplexer_6 (
    .in0(multiplexer_5_out), .in1(not_4_out), .out({NG, Out[14:0]}), .sel(NO));
  assign not_4_out = ~multiplexer_5_out;  // NOT_Gate not_4, 16 bits wide

  assign Out[15] = NG;
endmodule

module ALU_Test (
  input  in_1,
  input  in_2,
  input  in_3,
  input  in_4,
  input  in_5,
  input  in_6,
  input  [15:0] in_7,
  input  [15:0] in_8,
  output [15:0] out_9,
  output out_10,
  output out_11
);

  ALU alu_1 (
    .X(in_7), .Y(in_8), .Out(out_9), .NX_2(in_2), .ZY(in_3), .NY(in_4), .F(in_5), .NO(in_6), .NG(out_10),
    .ZR(out_11), .NX(in_1));
endmodule

module CPU (
  input  Clock,
  input  [15:0] Intruct,
  input  [15:0] InM,
  input  Reset,
  output [15:0] OutM,
  output writeM,
  output [14:0] addressM,
  output [14:0] PC
);

  wire alu_1_ng, alu_1_zr, controller_1_a, controller_1_alumux, controller_1_amux, controller_1_d,
       controller_1_pc, not_1_out;
  wire [5:0] controller_1_alu;
  wire [15:0] D_q, multiplexer_1_out, multiplexer_2_out;
  wire [15:15] A_q, PC_q;

  Controller controller_1 (
    .NG(alu_1_ng), .ZR(alu_1_zr), .Instruction(Intruct), .PC(controller_1_pc), .ALU(controller_1_alu),
    .WriteM(writeM), .D(controller_1_d), .A(controller_1_a), .AMux(controller_1_amux),
    .ALUMux(controller_1_alumux));
  not not_1 (not_1_out, controller_1_pc);
  Multiplexer #(.width(16), .enable("false")) multiplexer_1 (
    .in0(OutM), .in1(Intruct), .out(multiplexer_1_out), .sel(controller_1_amux));
  Register #(.width(16)) D (.D(OutM), .en(controller_1_d), .Q(D_q), .clk(Clock));  // open: clr
  Register #(.width(16)) A (
    .D(multiplexer_1_out), .en(controller_1_a), .Q({A_q[15], addressM}), .clk(Clock));  // open: clr
  Counter #(.width(16), .max('hffff)) u_PC (
    .load(controller_1_pc), .D({A_q[15], addressM}), .count(not_1_out), .Q({PC_q[15], PC}), .clk(Clock),
    .clr(Reset));  // open: carry
  Multiplexer #(.width(16), .enable("false")) multiplexer_2 (
    .in0({A_q[15], addressM}), .in1(InM), .out(multiplexer_2_out), .sel(controller_1_alumux));
  ALU alu_1 (
    .X(D_q), .Y(multiplexer_2_out), .Out(OutM), .NX_2(controller_1_alu[4]), .ZY(controller_1_alu[3]),
    .NY(controller_1_alu[2]), .F(controller_1_alu[1]), .NO(controller_1_alu[0]), .NG(alu_1_ng),
    .ZR(alu_1_zr), .NX(controller_1_alu[5]));
endmodule

module Jump (
  input  NG,
  input  ZR,
  input  [2:0] In,
  output Out
);

  wire and_1_out, and_2_out, and_3_out, and_4_out, and_5_out, and_6_out, demultiplexer_1_out0,
       demultiplexer_1_out1, demultiplexer_1_out2, demultiplexer_1_out3, demultiplexer_1_out4,
       demultiplexer_1_out5, demultiplexer_1_out6, demultiplexer_1_out7, not_1_out, not_2_out, not_3_out,
       not_4_out, not_5_out, not_6_out, or_1_out;

  Demultiplexer #(.select(3), .enable("false")) demultiplexer_1 (
    .out0(demultiplexer_1_out0), .out1(demultiplexer_1_out1), .out2(demultiplexer_1_out2),
    .out3(demultiplexer_1_out3), .out4(demultiplexer_1_out4), .out5(demultiplexer_1_out5),
    .out6(demultiplexer_1_out6), .out7(demultiplexer_1_out7), .in(1'b1), .sel(In));
  not not_1 (not_1_out, NG);
  not not_2 (not_2_out, ZR);
  not not_3 (not_3_out, NG);
  not not_4 (not_4_out, NG);
  not not_5 (not_5_out, ZR);
  not not_6 (not_6_out, ZR);
  or or_1 (or_1_out, NG, ZR);
  and and_1 (and_1_out, demultiplexer_1_out1, not_1_out, not_2_out);
  and and_2 (and_2_out, demultiplexer_1_out2, not_3_out, ZR);
  and and_3 (and_3_out, demultiplexer_1_out3, not_4_out);
  and and_4 (and_4_out, demultiplexer_1_out4, NG, not_5_out);
  and and_5 (and_5_out, demultiplexer_1_out5, not_6_out);
  and and_6 (and_6_out, demultiplexer_1_out6, or_1_out);
  or or_2 (Out, demultiplexer_1_out7, and_1_out, and_2_out, and_3_out, and_4_out, and_5_out, and_6_out);
endmodule

module Controller (
  input  NG,
  input  ZR,
  input  [15:0] Instruction,
  output PC,
  output [5:0] ALU,
  output WriteM,
  output D,
  output A,
  output AMux,
  output ALUMux
);

  wire and_4_out, jump_1_out;

  Jump jump_1 (.NG(NG), .ZR(ZR), .In(Instruction[2:0]), .Out(jump_1_out));
  and and_1 (PC, jump_1_out, Instruction[15]);
  and and_2 (WriteM, Instruction[3], Instruction[15]);
  and and_3 (D, Instruction[4], Instruction[15]);
  and and_4 (and_4_out, Instruction[5], Instruction[15]);
  not not_1 (AMux, Instruction[15]);
  or or_1 (A, and_4_out, AMux);
  and and_5 (ALUMux, Instruction[12], Instruction[15]);

  assign ALU = Instruction[11:6];
endmodule

module ROM_test (
  input  Clear,
  input  in_2
);

  wire clock_1_out, cpu_1_writem;
  wire [14:0] cpu_1_addressm, cpu_1_pc;
  wire [15:0] cpu_1_outm, memory_1_outm, rom_1_data;

  Clock clock_1 (.out(clock_1_out));
  ROM #(.addrWidth(15), .dataWidth(16)) rom_1 (.addr(cpu_1_pc), .data(rom_1_data), .sel(1'b1));
  // Probe on rom_1_data
  // Probe on cpu_1_pc
  CPU cpu_1 (
    .Clock(clock_1_out), .Intruct(rom_1_data), .InM(memory_1_outm), .OutM(cpu_1_outm), .writeM(cpu_1_writem),
    .addressM(cpu_1_addressm), .PC(cpu_1_pc), .Reset(Clear));
  Memory memory_1 (
    .InM(cpu_1_outm), .AddressM(cpu_1_addressm), .OutM(memory_1_outm), .Sel(1'b1), .WriteM(cpu_1_writem),
    .Clear(in_2), .Clock(clock_1_out));

  // Notes on the sheet:
  //   contents of rom_1 (hex, n*v repeats v):
  //   2 ec10 3 e090 0 e308
endmodule

module Memory (
  input  Clock,
  input  [15:0] InM,
  input  [14:0] AddressM,
  input  Sel,
  input  WriteM,
  input  Clear,
  output [15:0] OutM
);

  wire not_1_out;

  assign OutM = WriteM ? InM : 16'bz;  // Controlled_Buffer controlled_buffer_1
  RAM #(.addrWidth(15), .dataWidth(16)) ram_1 (
    .addr(AddressM), .data(OutM), .sel(Sel), .clk(Clock), .ld(not_1_out), .clr(Clear));
  not not_1 (not_1_out, WriteM);
endmodule
